# Fritzing sketch hmcduino (saved by Fritzing 0.5.2b)
breadboards: 1

parts:
  Arduino1 = Arduino
  IC1 = IC, DIP package, 6 pins [chip_label=X9C503 spacing=300mil]
  IC2 = IC, DIP package, 14 pins [chip_label=IC spacing=300mil]
  TRS1 = Stereo Jack (TRS) 3.5mm [package="PG203J [THT]"]

nets:
  N1: Arduino1.GND, IC1.pin3, IC2.pin7, TRS1.Ring
  N2: Arduino1.D7, IC2.pin13
  N3: Arduino1.D6, IC1.pin1
  N4: Arduino1.D5, IC1.pin2
  N5: Arduino1.D4, IC1.pin5
  N6: Arduino1.+5V, IC1.pin6, IC2.pin14
  N7: IC1.pin4, IC2.pin2, TRS1.Sleeve
  N8: IC2.pin1, TRS1.Tip
